# Fritzing sketch temperatura2-buttons (saved by Fritzing 0.8.7b)
circuit board: 5.77848cm x 2.00579cm
breadboards: 1

parts:
  S1 = Pushbutton [package="[THT]"]
  S2 = Pushbutton [package="[THT]"]
  S3 = Pushbutton [package="[THT]"]
  S4 = Pushbutton [package="[THT]"]
  J1 = male pin header, 3 pins [form="♂ (male)"]
  R3 = Resistor [tolerance=±5% resistance=10k package=THT]
  R4 = Resistor [tolerance=±5% resistance=10k package=THT]
  R2 = Resistor [tolerance=±5% resistance=10k package=THT]
  R1 = Resistor [tolerance=±5% resistance=10k package=THT]

nets:
  N1: S1.Pin_1, S1.Pin_2, R1.Pin_0
  N2: S1.Pin_3, S1.Pin_4, S2.Pin_3, S2.Pin_4, S3.Pin_3, S3.Pin_4, S4.Pin_3, S4.Pin_4, J1.pin1
  N3: S2.Pin_1, S2.Pin_2, R2.Pin_0, R1.Pin_1
  N4: S3.Pin_1, S3.Pin_2, R3.Pin_0, R2.Pin_1
  N5: S4.Pin_1, S4.Pin_2, J1.pin3, R3.Pin_1, R4.Pin_0
  N6: J1.pin2, R4.Pin_1
