# Fritzing sketch temperatura2 (saved by Fritzing 0.9.0b)
circuit board: 6cm x 10cm
breadboards: 2

parts:
  R5 = Resistor [tolerance=±10% resistance=1.5k package=THT]
  D3 = Rectifier Diode [part_number=1N4007 package="300 mil [THT]"]
  Q2 = NPN-Transistor [package="TO92 [THT]"]
  R4 = Resistor [tolerance=±10% resistance=1.5k package=THT]
  D2 = Rectifier Diode [part_number=1N4007 package="300 mil [THT]"]
  Q1 = NPN-Transistor [package="TO92 [THT]"]
  U2 = atmega328 [package=dip]
  S1 = Pushbutton [package="[THT]"]
  XTAL1 = Crystal [frequency="16 Mhz" package=THT]
  C4 = Ceramic Capacitor [capacitance=27pF voltage=50V package="200 mil [THT, multilayer]"]
  C3 = Ceramic Capacitor [capacitance=27pF voltage=50V package="200 mil [THT, multilayer]"]
  R2 = Resistor [tolerance=±5% resistance=1k package=THT]
  C1 = Electrolytic Capacitor [capacitance=47µF voltage=35V package="100 mil [THT, electrolytic]"]
  U1 = Voltage Regulator - 5V [package="TO220 [THT]"]
  C2 = Electrolytic Capacitor [capacitance=47µF voltage=16V package="100 mil [THT, electrolytic]"]
  LED1 = LED - 5mm [color="Red (633nm)" package="5 mm [THT]"]
  R1 = Resistor [tolerance=±5% resistance=330 package=THT]
  J1 = Power Jack [package=power_jack_pth]
  D1 = Rectifier Diode [part_number=1N4007 package="300 mil [THT]"]
  J3 = male pin header, 3 pins [form="♂ (male)"]
  R6 = Resistor [tolerance=±5% resistance=330 package=THT]
  LED3 = LED - 5mm [color="Yellow (595nm)" package="5 mm [THT]"]
  R3 = Resistor [tolerance=±5% resistance=4.7k package=THT]
  C5 = Ceramic Capacitor [capacitance=100nF voltage=35V package="100 mil [THT, multilayer]"]
  C6 = Ceramic Capacitor [capacitance=100nF package="100 mil [THT, multilayer]"]
  J8 = shrouded pin header, 10 pins [form="♂ (shrouded male)"]
  K2 = Relay T73
  J6 = screw terminal, 3 pins
  J5 = screw terminal, 3 pins
  J9 = male pin header, 3 pins [form="♂ (male)"]
  K1 = Relay T73

nets (from the pcb view):
  N1: R5.Pin_0, Q2.B
  N2: R5.Pin_1, U2.D3_(PWM)
  N3: D3.cathode, D2.cathode, J1.PWR, D1.anode, K2.C2, K1.C2
  N4: D3.anode, Q2.E, K2.C1
  GND: Q2.C, Q1.C, U2.GND, S1.Pin_3, S1.Pin_4, C4.1, C3.1, C1.-, U1.GND, C2.-, LED1.cathode, J1.GND, J1.GNDBREAK, J3.pin2, LED3.cathode, C5.1, C6.0, J8.pin8, J8.pin9, J8.pin10, J9.pin3
  N5: R4.Pin_0, Q1.B
  N6: R4.Pin_1, U2.D2
  N7: D2.anode, Q1.E, K1.C1
  N8: U2.RESET, S1.Pin_1, S1.Pin_2, R2.Pin_0
  N9: U2.VCC, U2.AVCC, R2.Pin_1, U1.output_voltage, C2.+, R1.Pin_0, J3.pin1, R3.Pin_0, C6.1, J8.pin1, J9.pin2
  N10: U2.XLAT1, XTAL1.pin_1, C3.0
  N11: U2.XLAT2, XTAL1.pin_0, C4.0
  N12: U2.D5_(PWM), J8.pin7
  N13: U2.D6_(PWM), J8.pin6
  N14: U2.D7, J8.pin5
  N15: U2.D8, J8.pin4
  N16: U2.D10_(PWM), R3.Pin_1, J9.pin1
  N17: U2.D11_(PWM), J8.pin2
  N18: U2.D12, J8.pin3
  N19: U2.D13, R6.Pin_0
  N20: U2.A0, J3.pin3
  N21: C1.+, U1.input_voltage, D1.cathode, C5.0
  N22: LED1.anode, R1.Pin_1
  N23: R6.Pin_1, LED3.anode
  N24: K2.COM, J6.pin2
  N25: K2.NO, J6.pin3
  N26: K2.NC, J6.pin1
  N27: J5.pin1, K1.NC
  N28: J5.pin2, K1.COM
  N29: J5.pin3, K1.NO

custom parts:
  Relay T73: An T73 Mini PCB Relay
